# Fritzing sketch SCATschematic (saved by Fritzing 0.8.7b)
breadboards: 1

parts:
  U1 = Spark Core (v1.0)
  T1 = TMP36 Temperature Sensor [package="TO92 [THT]"]
  C1 = Capacitor [package=cap-pth-small2]

nets:
  N1: U1.A2, U1.3V3
  N2: U1.A3, U1.A6
  N3: U1.A4, T1.Vout, C1.2
  N4: U1.A5, U1.VIN, T1.+Vs
  GND: U1.GND, T1.GND, C1.1

notes:
  to relay

custom parts:
  Spark Core (v1.0): The Spark Core is a tiny Wi-Fi development board that makes it easy to create internet-connected hardware. The Core is all you need to get started; power it over USB and in minutes you'll be controlling LEDs, switches and motors and collecting data from sensors over the internet! It has 8 digital I/O pins, 8 analog I/O pins, 8 PWM pins; UART (Serial), SPI, I2C, and JTAG peripherals available.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
